# Fritzing sketch LevelController_TwoRelay_V0.001 (saved by Fritzing 0.9.2b)
circuit board: 14.9361cm x 8.93338cm
breadboards: 1

parts:
  J13 = Power Jack [package=power_jack_slot]
  10uF = Electrolytic Capacitor [capacitance=1µF package="100 mil [THT, electrolytic]"]
  7805 = Voltage Regulator [package=to220-igo]
  Pad17 = Pad [width=2.5 height=2.5 connect=center]
  Pad18 = Pad [width=2.5 height=2.5 connect=center]
  NC2 = Pad [width=2.5 height=2.5 connect=center]  # not connected
  NO2 = Pad [width=2.5 height=2.5 connect=center]
  Pad19 = Pad [width=2.5 height=2.5 connect=center]
  C9 = Ceramic Capacitor [capacitance=100nF package="100 mil [THT, multilayer]"]
  5V = female pin header, 4 pins [form="♀ (female)"]
  ISP = female pin header, 6 pins [form="♀ (female)"]
  OUTPUT = female pin header, 6 pins [form="♀ (female)"]
  ATmega8 = MICROCONTROLLER [package=dil28-3-simon]
  INPUT1 = female pin header, 5 pins [form="♀ (female)"]
  Pad20 = Pad [width=2.5 height=2.5 connect=center]
  Pad21 = Pad [width=2.5 height=2.5 connect=center]
  NC3 = Pad [width=2.5 height=2.5 connect=center]  # not connected
  NO3 = Pad [width=2.5 height=2.5 connect=center]
  Pad22 = Pad [width=2.5 height=2.5 connect=center]
  R38 = Resistor [tolerance=±5% resistance=220 package=THT]
  LED1 = LED - 3mm [color="Red (633nm)" package="3 mm [THT]"]
  IC1 = ULN2803A [package=THT]
  Relay_Socket2 = screw terminal, 2 pins
  Relay_Socket1 = screw terminal, 2 pins
  R41 = Resistor [tolerance=±5% resistance=220 package=THT]
  R42 = Resistor [tolerance=±5% resistance=220 package=THT]
  R43 = Resistor [tolerance=±5% resistance=220 package=THT]
  R44 = Resistor [tolerance=±5% resistance=220 package=THT]
  R45 = Resistor [tolerance=±5% resistance=220 package=THT]
  R46 = Resistor [tolerance=±5% resistance=220 package=THT]
  LED2 = LED - 3mm [color="Red (633nm)" package="3 mm [THT]"]
  LED3 = LED - 3mm [color="Red (633nm)" package="3 mm [THT]"]
  LED5 = LED - 3mm [color="Red (633nm)" package="3 mm [THT]"]
  LED6 = LED - 3mm [color="Red (633nm)" package="3 mm [THT]"]
  LED4 = LED - 3mm [color="Red (633nm)" package="3 mm [THT]"]
  LED7 = LED - 3mm [color="Red (633nm)" package="3 mm [THT]"]
  IN-out = screw terminal, 6 pins
  Relay_Socket3 = screw terminal, 2 pins  # not connected
  GND = female pin header, 4 pins [form="♀ (female)"]

nets:
  GND: J13.GNDBREAK, J13.GND, 10uF.-, 7805.GND, C9.0, ISP.pin1, ATmega8.GND, ATmega8.AGND, LED1.cathode, IC1.In_8, IC1.0V, IN-out.pin3, GND.pin1, GND.pin2, GND.pin3, GND.pin4
  VCC: J13.PWR, 10uF.+, 7805.IN
  12V/5V: 7805.OUT, Pad17.pad, C9.1, 5V.pin1, 5V.pin2, 5V.pin3, 5V.pin4, ISP.pin6, ATmega8.VCC, Pad20.pad, R38.Pin_1, IC1.COM_-_Common, IC1.Out_8, LED2.anode, LED3.anode, LED5.anode, LED6.anode, LED4.anode, LED7.anode, IN-out.pin1, IN-out.pin2
  IC0: Pad18.pad, IC1.Out_1, R41.Pin_0
  N1: NO2.pad, Relay_Socket1.pin2
  N2: Pad19.pad, Relay_Socket1.pin1
  SCK: ISP.pin2, ATmega8.PB5(SCK)
  MISO: ISP.pin3, ATmega8.PB4(MISO)
  MOSI: ISP.pin4, ATmega8.PB3(MOSI_OC2)
  RST: ISP.pin5, ATmega8.PC6(_RESET)
  OUT5: OUTPUT.pin1, ATmega8.PC5(ADC5_SCL), R45.Pin_1
  OUT4: OUTPUT.pin2, ATmega8.PC4(ADC4_SDA), R44.Pin_1
  OUT3: OUTPUT.pin3, ATmega8.PC3(ADC3), R43.Pin_0
  OUT2: OUTPUT.pin4, ATmega8.PC2(ADC2), R46.Pin_1
  OUT1: OUTPUT.pin5, ATmega8.PC1(ADC1), IC1.In_1
  OUT0: OUTPUT.pin6, ATmega8.PC0(ADC0), IC1.In_2
  IN0: ATmega8.PD4(XCK_T0)
  IN1: ATmega8.PD5(T1), INPUT1.pin5, IC1.Out_3
  IN2: ATmega8.PD6(AIN0), INPUT1.pin4, IC1.Out_4
  IN3: ATmega8.PD7(AIN1), INPUT1.pin3, IC1.Out_5
  IN4: ATmega8.PB0(ICP), INPUT1.pin2
  IN5: INPUT1.pin1
  IC1: Pad21.pad, IC1.Out_2, R42.Pin_0
  N3: NO3.pad, Relay_Socket2.pin2
  N4: Pad22.pad, Relay_Socket2.pin1
  N5: R38.Pin_0, LED1.anode
  L0: IC1.In_3, IN-out.pin6
  L1: IC1.In_4, IN-out.pin5
  L2: IC1.In_5, IN-out.pin4
  N6: R41.Pin_1, LED2.cathode
  N7: R42.Pin_1, LED3.cathode
  N8: R43.Pin_1, LED4.cathode
  N9: R44.Pin_0, LED5.cathode
  N10: R45.Pin_0, LED6.cathode
  N11: R46.Pin_0, LED7.cathode

notes:
  INPUT AND LEVEL INDICATOR
  POWER LED CKT
  12-5 VOLT REGULATOR
  Atmega8 Controller CKT
  Level Controller BV1.0
  COM
  NO
  NC
  VCC
  GND
