# Fritzing sketch LevelController_TwoRelay_V1.001 (saved by Fritzing 0.9.2b)
circuit board: 10.8676cm x 7.5421cm
breadboards: 1

parts:
  J13 = Power Jack [package=power_jack_slot]
  10uF = Electrolytic Capacitor [capacitance=1µF package="100 mil [THT, electrolytic]"]
  7805 = Voltage Regulator [package=to220-igo]
  C9 = Ceramic Capacitor [capacitance=100nF package="100 mil [THT, multilayer]"]
  ISP = female pin header, 6 pins [form="♀ (female)"]
  OUTPUT = female pin header, 6 pins [form="♀ (female)"]
  ATmega8 = MICROCONTROLLER [package=dil28-3-simon]
  R38 = Resistor [tolerance=±5% resistance=220 package=THT]
  LED1 = LED - 3mm [color="Red (633nm)" package="3 mm [THT]"]
  IC1 = ULN2803A [package=THT]
  R41 = Resistor [tolerance=±5% resistance=220 package=THT]
  R42 = Resistor [tolerance=±5% resistance=220 package=THT]
  R43 = Resistor [tolerance=±5% resistance=220 package=THT]
  R44 = Resistor [tolerance=±5% resistance=220 package=THT]
  R45 = Resistor [tolerance=±5% resistance=220 package=THT]
  R46 = Resistor [tolerance=±5% resistance=220 package=THT]
  GND = female pin header, 4 pins [form="♀ (female)"]
  J14 = female pin header, 4 pins [form="♀ (female)"]
  J16 = female pin header, 2 pins [form="♀ (female)"]
  J17 = female pin header, 3 pins [form="♀ (female)"]
  J18 = female pin header, 4 pins [form="♀ (female)"]
  5V = female pin header, 4 pins [form="♀ (female)"]
  Relay_Socket3 = screw terminal, 6 pins
  Pad23 = Pad [width=2.5 height=2.5 connect=center]
  Pad24 = Pad [width=2.5 height=2.5 connect=center]
  Pad25 = Pad [width=2.5 height=2.5 connect=center]
  Pad26 = Pad [width=2.5 height=2.5 connect=center]
  NC4 = Pad [width=2.5 height=2.5 connect=center]
  NC5 = Pad [width=2.5 height=2.5 connect=center]
  NO4 = Pad [width=2.5 height=2.5 connect=center]
  NO5 = Pad [width=2.5 height=2.5 connect=center]
  Pad27 = Pad [width=2.5 height=2.5 connect=center]
  Pad28 = Pad [width=2.5 height=2.5 connect=center]
  IN-out = screw terminal, 6 pins
  J15 = female pin header, 3 pins [form="♀ (female)"]

nets:
  GND: J13.GNDBREAK, J13.GND, 10uF.-, 7805.GND, C9.0, ISP.pin1, ATmega8.GND, ATmega8.AGND, LED1.cathode, IC1.In_8, IC1.0V, GND.pin1, GND.pin2, GND.pin3, GND.pin4, IN-out.pin2
  VCC: J13.PWR, 10uF.+, 7805.IN
  5V: 7805.OUT, C9.1, ISP.pin6, ATmega8.VCC, R38.Pin_1, IC1.COM_-_Common, IC1.Out_8, J17.pin3, 5V.pin1, 5V.pin2, 5V.pin3, 5V.pin4, Pad23.pad, Pad24.pad, IN-out.pin1, J15.pin3
  SCK: ISP.pin2, ATmega8.PB5(SCK)
  MISO: ISP.pin3, ATmega8.PB4(MISO)
  MOSI: ISP.pin4, ATmega8.PB3(MOSI_OC2)
  RST: ISP.pin5, ATmega8.PC6(_RESET)
  OUT5: OUTPUT.pin1, ATmega8.PC5(ADC5_SCL), R45.Pin_1
  OUT4: OUTPUT.pin2, ATmega8.PC4(ADC4_SDA), R44.Pin_1
  OUT3: OUTPUT.pin3, ATmega8.PC3(ADC3), R43.Pin_0
  OUT2: OUTPUT.pin4, ATmega8.PC2(ADC2), R46.Pin_1
  OUT1: OUTPUT.pin5, ATmega8.PC1(ADC1), IC1.In_1
  OUT0: OUTPUT.pin6, ATmega8.PC0(ADC0), IC1.In_2
  N1: ATmega8.PD0(RXD), J18.pin4
  N2: ATmega8.PD1(TXD), J18.pin3
  N3: ATmega8.PD2(INT0), J18.pin2
  N4: ATmega8.PD3(INT1), J18.pin1
  IN0: ATmega8.PD4(XCK_T0)
  IN1: ATmega8.PD5(T1), IC1.Out_3
  IN2: ATmega8.PD6(AIN0), IC1.Out_4
  IN3: ATmega8.PD7(AIN1), IC1.Out_5
  IN4: ATmega8.PB0(ICP), IC1.Out_6
  OUT6: ATmega8.PB1(OC1A), J16.pin1
  OUT7: ATmega8.PB2(SS_OC1B), J16.pin2
  N5: R38.Pin_0, LED1.anode
  L0: IC1.In_3, IN-out.pin6
  L1: IC1.In_4, IN-out.pin5
  L2: IC1.In_5, IN-out.pin4
  L3: IC1.In_6, IN-out.pin3
  IC1/M1: IC1.Out_2, R42.Pin_0, J17.pin1, Pad26.pad
  IC0/M0: IC1.Out_1, R41.Pin_0, J17.pin2, Pad25.pad
  N6: R41.Pin_1, J15.pin2
  N7: R42.Pin_1, J15.pin1
  N8: R43.Pin_1, J14.pin3
  N9: R44.Pin_0, J14.pin2
  N10: R45.Pin_0, J14.pin1
  N11: R46.Pin_0, J14.pin4
  N12: Relay_Socket3.pin1, NC5.pad
  N13: Relay_Socket3.pin2, Pad28.pad
  N14: Relay_Socket3.pin3, NO5.pad
  N15: Relay_Socket3.pin4, NC4.pad
  N16: Relay_Socket3.pin5, Pad27.pad
  N17: Relay_Socket3.pin6, NO4.pad

notes:
  INPUT AND LEVEL INDICATOR
  POWER LED CKT
  12-5 VOLT REGULATOR
  Atmega8 Controller CKT
  M0
  M1
  vcc
  GND
  COM
  VCC
  NO
  NC
