# Fritzing sketch LevelController_TwoRelay_V1.001_LED_design (saved by Fritzing 0.9.2b)
circuit board: 4.50687cm x 5.27436cm
breadboards: 1

parts:
  J14 = female pin header, 4 pins [form="♀ (female)"]
  J15 = female pin header, 3 pins [form="♀ (female)"]
  LED2 = LED - 3mm [color="Red (633nm)" package="3 mm [THT]"]
  LED1 = LED - 3mm [color="Red (633nm)" package="3 mm [THT]"]
  LED3 = LED - 3mm [color="Red (633nm)" package="3 mm [THT]"]
  LED4 = LED - 3mm [color="Red (633nm)" package="3 mm [THT]"]
  LED5 = LED - 3mm [color="Red (633nm)" package="3 mm [THT]"]
  LED6 = LED - 3mm [color="Red (633nm)" package="3 mm [THT]"]
  J16 = female pin header, 4 pins [form="♀ (female)"]

nets:
  MS: J14.pin1, LED4.cathode, J16.pin1
  L2: J14.pin2, LED3.cathode, J16.pin2
  L1: J14.pin3, LED2.cathode, J16.pin3
  L0: J14.pin4, LED1.cathode, J16.pin4
  N1: J15.pin1, LED6.cathode
  N2: J15.pin2, LED5.cathode
  5V: J15.pin3, LED2.anode, LED1.anode, LED3.anode, LED4.anode, LED5.anode, LED6.anode

notes:
  INPUT AND LEVEL INDICATOR
  GND
  COM
  VCC
  NO
  NC
  M0
  M1
