# Fritzing sketch LevelMonitorWithBuzzer (saved by Fritzing 0.9.2b)
circuit board: 7.29258cm x 6.57996cm
breadboards: 1

parts:
  J13 = Power Jack [package=power_jack_slot]
  10uF = Electrolytic Capacitor [capacitance=1µF package="100 mil [THT, electrolytic]"]
  7805 = Voltage Regulator [package=to220-igo]
  C9 = Ceramic Capacitor [capacitance=100nF package="100 mil [THT, multilayer]"]
  IC1 = ULN2803A [package=THT]
  IN-out1 = screw terminal, 3 pins
  IN-out2 = screw terminal, 3 pins
  R39 = Resistor [tolerance=±5% resistance=220 package=THT]
  R40 = Resistor [tolerance=±5% resistance=220 package=THT]
  R42 = Resistor [tolerance=±5% resistance=220 package=THT]
  R41 = Resistor [tolerance=±5% resistance=220 package=THT]
  J14 = female pin header, 4 pins [form="♀ (female)"]
  J15 = female pin header, 4 pins [form="♀ (female)"]
  R43 = Resistor [tolerance=±5% resistance=220 package=THT]
  SPKR1 = Loudspeaker
  SPKR2 = Loudspeaker

nets:
  GND: J13.GNDBREAK, J13.GND, 10uF.-, 7805.GND, C9.0, IC1.In_8, IC1.0V, J15.pin3
  VCC: J13.PWR, 10uF.+, 7805.IN
  5V: 7805.OUT, C9.1, IC1.COM_-_Common, IC1.Out_8, IN-out1.pin1, IN-out2.pin1, J15.pin4, R43.Pin_0, SPKR1.pin1, SPKR2.pin1
  L0: IC1.In_1, IN-out1.pin3
  L1: IC1.In_2, IN-out1.pin2
  L10: IC1.In_6, IN-out2.pin3
  L11: IC1.In_7, IN-out2.pin2
  OUT11: IC1.Out_7, R40.Pin_0, SPKR2.pin2
  OUT10: IC1.Out_6, R39.Pin_0
  OUT1: IC1.Out_2, R42.Pin_0, SPKR1.pin2
  OUT0: IC1.Out_1, R41.Pin_0
  LED10: R39.Pin_1, J14.pin3
  LED11: R40.Pin_1, J14.pin4
  LED1: R42.Pin_1, J14.pin2
  LED0: R41.Pin_1, J14.pin1
  N1: J15.pin1, R43.Pin_1

notes:
  INPUT AND LEVEL INDICATOR
  POWER LED CKT
  12-5 VOLT REGULATOR
  M0
  M1
  vcc
