# Fritzing sketch LevelMonitorWithBuzzer_LED_Interface (saved by Fritzing 0.9.2b)
circuit board: 3.03231cm x 4.83302cm
breadboards: 1

parts:
  J14 = female pin header, 4 pins [form="♀ (female)"]
  J15 = female pin header, 4 pins [form="♀ (female)"]
  PWR-LED = LED - 3mm [color="Red (633nm)" package="3 mm [THT]"]
  PWR-LED1 = LED - 3mm [color="Red (633nm)" package="3 mm [THT]"]
  PWR-LED3 = LED - 3mm [color="Red (633nm)" package="3 mm [THT]"]
  PWR-LED4 = LED - 3mm [color="Red (633nm)" package="3 mm [THT]"]
  J16 = female pin header, 4 pins [form="♀ (female)"]
  J17 = female pin header, 4 pins [form="♀ (female)"]
  PWR-LED2 = LED - 3mm [color="Red (633nm)" package="3 mm [THT]"]

nets:
  LED0: J14.pin1, PWR-LED1.cathode, J16.pin1
  LED1: J14.pin2, J16.pin2, PWR-LED2.cathode
  LED10: J14.pin3, PWR-LED3.cathode, J16.pin3
  LED11: J14.pin4, PWR-LED4.cathode, J16.pin4
  PWR-LED: J15.pin1, PWR-LED.anode, J17.pin1
  N1: J15.pin2, J17.pin2
  GND: J15.pin3, PWR-LED.cathode, J17.pin3
  5V: J15.pin4, PWR-LED1.anode, PWR-LED3.anode, PWR-LED4.anode, J17.pin4, PWR-LED2.anode

notes:
  INPUT AND LEVEL INDICATOR
  POWER LED CKT
